# Fritzing sketch Untitled Sketch (saved by Fritzing 0.9.3b)
breadboards: 1

parts:
  Teensy++1 = Teensy++ 2.0
  T1 = LM35 Temperature Sensor [package="TO92 [THT]"]
  Part2 = Bluetooth HC-05 Macho  # not connected
  Part3 = IMU Analog Combo Board - 5 Degrees of Freedom
  Part4 = IMU Digital Combo Board 6DOF

nets:
  N1: Teensy++1.GND#0, T1.GND, Part3.XRATE
  N2: Teensy++1.D0, Part3.YRATE, Part4.GND
  N3: Teensy++1.D1, Part3.VREF, Part4.SDA
  N4: Teensy++1.F7, T1.+Vs
  3.3V: Teensy++1.VCC, T1.Vout, Part3.3.3V, Part4.3.3V, Part4.INT0
